# Fritzing sketch allConnection (saved by Fritzing 0.9.3b)

parts:
  Part2 = InvenSense MPU6050
  R1 = Basic Flex Resistor
  R2 = Basic Flex Resistor
  R3 = Basic Flex Resistor
  R4 = Basic Flex Resistor
  R5 = Basic Flex Resistor
  Part3 = Bluetooth HC-05 Macho
  Part1 = Arduino Nano (Rev3.0)
  R11 = Resistor [tolerance=±5% resistance=220 package=THT]
  R12 = Resistor [tolerance=±5% resistance=220 package=THT]
  Raspberry_Pi_1 = Raspberry Pi 3 [part_number=RPI-3-V1.2]  # not connected
  R13 = Resistor [tolerance=±5% resistance=220 package=THT]

nets:
  VCC: Part2.VCC, Part3.VCC, Part1.5V
  GND: Part2.GND, Part3.GND, Part1.GND, R11.Pin_0, R13.Pin_1
  N1: Part2.SCL, Part1.A6
  N2: Part2.SDA, Part1.A5
  N3: Part2.INT, Part1.D2
  N4: R1.Pin_2, R2.Pin_2, R3.Pin_2, R4.Pin_2, R5.Pin_2, R13.Pin_0
  N5: R5.pin_1, Part1.3V3
  N6: Part3.TXD, Part1.D0/RX
  N7: Part3.RXD, R11.Pin_1, R12.Pin_1
  N8: Part1.D1/TX, R12.Pin_0
